# Fritzing sketch Magnetic Stirrer (saved by Fritzing 0.9.3b)
breadboards: 1

parts:
  Fan = Fan - 4pin PWM [package=THT]
  R1 = Rotary Potentiometer (Large) [maximum_resistance=10kΩ package=THT]
  Power_Jack_(12V) = Power Jack [package=power_jack_pth]
  Arduino_Nano = Arduino Nano (Rev3.0)
  R2 = Resistor [tolerance=±5% resistance=470 package=THT]

nets:
  12V: Fan.12V, Power_Jack_(12V).PWR, Arduino_Nano.VIN
  GND: Fan.GND, R1.leg2, Power_Jack_(12V).GND, Arduino_Nano.GND
  N1: Fan.RPM_Signal_(out), Arduino_Nano.D2, R2.Pin_0
  N2: Fan.PWM_Signal_(in), Arduino_Nano.D3
  N3: R1.leg1, Arduino_Nano.5V, R2.Pin_1
  N4: R1.wiper, Arduino_Nano.A0

custom parts:
  Fan - 4pin PWM: 4 pin fan with pwm and rpm

// code stored in the sketch: Magnetic Stirrer.ino

// PINS
float potValue   = 0;  // A0 fom the potentiometer, speed control
int   fanSensor  = 0;  // Pulse indicating current RPM of the fan interrupt 0 = D2 (digital pin 2)
float fanPWM     = 3;  // PWM pin writes speed out to the fan

// Other
int   fanDivider = 4;  // Number of pulses per complete revolution
unsigned long SensorPulseWidth;
unsigned long counter = 0;
unsigned long counter2 = 0;
volatile int pwm_value = 0;
volatile int prev_time = 0;

// the setup routine runs once when you press reset:
void setup() {
  // initialize serial communication at 9600 bits per second:
  Serial.begin(9600);
  pinMode(potValue, INPUT);
  pinMode(fanSensor, INPUT);
  digitalWrite(fanSensor, HIGH);
  pinMode(fanPWM, OUTPUT);

  analogWrite(fanPWM, 0.0); // start off slow!

  attachInterrupt(fanSensor, rising, RISING);
}

// the loop routine runs over and over again forever:
void loop() {
  // read the input on analog pin 0:
  int sensorValue = analogRead(potValue);
  // Convert the analog reading (which goes from 0 - 1023) to a voltage (0 - 5V):
  float voltage = sensorValue * (5.0 / 1023.0);
  // convert the analog reading (which goes from 0 - 1023) to a fan speed (0 - 255): 
  float fanSpeed = sensorValue / 4.0;
  
  // write it out to the PWM pin:
  analogWrite(fanPWM, fanSpeed);

  counter++;
  counter2++;

  if (counter >= 500)
  {
    // print out the value you read:
    //Serial.println(String(voltage) + " " + String(fanSpeed));
    
    //SensorPulseWidth = pulseIn(fanSensor, LOW, 100000); // read pulse width, 1000 microsecond timeout
    SensorPulseWidth = pwm_value;
    double frequency = 1000000/SensorPulseWidth;  // 1000000 microsec / SensorPulsTijd = aantal microsec per puls.

    /*Serial.print("Pulse width in microsec.  = ");
    Serial.println(SensorPulseWidth);
    Serial.print("Rotatietijd in microsec.  = ");
    Serial.println(SensorPulseWidth*fanDivider);
    Serial.print("Frequency in Herz         = ");
    Serial.println(frequency/fanDivider, 0); */
    Serial.print("Revolutions per Minute    = ");
    Serial.println(frequency/fanDivider*60);
    //Serial.println();
    //Serial.println();
    counter = 0; 
  }

  if (counter2 >= 50000)
  {
    pwm_value = 0;
    counter2 = 0;
  }
}

void rising() {
  attachInterrupt(fanSensor, falling, FALLING);
  prev_time = micros();
}
 
void falling() {
  attachInterrupt(fanSensor, rising, RISING);
  pwm_value = micros()-prev_time;
  //Serial.println(pwm_value);
}
